// Logisim project NAND2Tetris_logisim.circ as structural Verilog: 10 circuits, main circuit main
module main (
  input  in_1,
  input  in_2,
  output out_3,
  output out_4
);

  HalfAdder halfadder_1 (.a(in_1), .b(in_2), .sum(out_3), .carry(out_4));
endmodule

module Mux4Way16 (
  input  [15:0] a16,
  input  [15:0] b16,
  input  [15:0] c16,
  input  [15:0] d16,
  input  [1:0] sel2,
  output [15:0] out16
);

  wire [15:0] multiplexer_1_out, multiplexer_2_out;

  Multiplexer #(.width(16), .enable("false")) multiplexer_1 (
    .in0(a16), .in1(b16), .out(multiplexer_1_out), .sel(sel2[0]));
  Multiplexer #(.width(16), .enable("false")) multiplexer_2 (
    .in0(c16), .in1(d16), .out(multiplexer_2_out), .sel(sel2[0]));
  Multiplexer #(.width(16), .enable("false")) multiplexer_3 (
    .in0(multiplexer_1_out), .in1(multiplexer_2_out), .out(out16), .sel(sel2[1]));
endmodule

module Mux8Way16 (
  input  [15:0] a16,
  input  [15:0] b16,
  input  [15:0] c16,
  input  [15:0] d16,
  input  [15:0] e16,
  input  [15:0] f16,
  input  [15:0] g16,
  input  [15:0] h16,
  input  [2:0] sel3,
  output [15:0] out16
);

  wire [15:0] mux4way16_1_out16, mux4way16_2_out16;

  Mux4Way16 mux4way16_1 (.a16(a16), .b16(b16), .c16(c16), .d16(d16), .sel2(sel3[1:0]), .out16(mux4way16_1_out16));
  Mux4Way16 mux4way16_2 (.a16(e16), .b16(f16), .c16(g16), .d16(h16), .sel2(sel3[1:0]), .out16(mux4way16_2_out16));
  Multiplexer #(.width(16), .enable("false")) multiplexer_1 (
    .in0(mux4way16_1_out16), .in1(mux4way16_2_out16), .out(out16), .sel(sel3[2]));
endmodule

module Or8Way (
  input  [7:0] in8,
  output out1
);

  wire or_1_out, or_2_out, or_3_out, or_4_out, or_5_out, or_6_out;

  or or_1 (or_1_out, in8[0], in8[1]);
  or or_2 (or_2_out, in8[2], in8[3]);
  or or_3 (or_3_out, in8[4], in8[5]);
  or or_4 (or_4_out, in8[6], in8[7]);
  or or_5 (or_5_out, or_1_out, or_2_out);
  or or_6 (or_6_out, or_3_out, or_4_out);
  or or_7 (out1, or_5_out, or_6_out);
endmodule

module DMux4Way (
  input  in1,
  input  [1:0] sel2,
  output a1,
  output b1,
  output c1,
  output d1
);

  wire demultiplexer_1_out0, demultiplexer_1_out1;

  Demultiplexer #(.enable("false")) demultiplexer_1 (
    .out0(demultiplexer_1_out0), .out1(demultiplexer_1_out1), .in(in1), .sel(sel2[1]));
  Demultiplexer #(.enable("false")) demultiplexer_2 (.out0(a1), .out1(b1), .in(demultiplexer_1_out0), .sel(sel2[0]));
  Demultiplexer #(.enable("false")) demultiplexer_3 (.out0(c1), .out1(d1), .in(demultiplexer_1_out1), .sel(sel2[0]));
endmodule

module DMux8Way (
  input  in1,
  input  [2:0] sel3,
  output a1,
  output b1,
  output c1,
  output d1,
  output e1,
  output f1,
  output g1,
  output h1
);

  wire demultiplexer_1_out0, demultiplexer_1_out1;

  Demultiplexer #(.enable("false")) demultiplexer_1 (
    .out0(demultiplexer_1_out0), .out1(demultiplexer_1_out1), .in(in1), .sel(sel3[2]));
  DMux4Way dmux4way_1 (.in1(demultiplexer_1_out0), .sel2(sel3[1:0]), .a1(a1), .b1(b1), .c1(c1), .d1(d1));
  DMux4Way dmux4way_2 (.in1(demultiplexer_1_out1), .sel2(sel3[1:0]), .a1(e1), .b1(f1), .c1(g1), .d1(h1));
endmodule

module HalfAdder (
  input  a,
  input  b,
  output sum,
  output carry
);

  xor xor_1 (sum, a, b);
  and and_1 (carry, a, b);
endmodule

module FullAdder (
  input  a,
  input  b,
  input  c,
  output sum,
  output carry
);

  wire halfadder_1_carry, halfadder_1_sum, halfadder_2_carry;

  HalfAdder halfadder_1 (.a(a), .b(b), .sum(halfadder_1_sum), .carry(halfadder_1_carry));
  HalfAdder halfadder_2 (.a(halfadder_1_sum), .b(c), .sum(sum), .carry(halfadder_2_carry));
  xor xor_1 (carry, halfadder_2_carry, halfadder_1_carry);
endmodule

module Add16 (
  input  [15:0] a16,
  input  [15:0] b16,
  output [15:0] out16
);

  wire fulladder_1_carry, fulladder_2_carry, fulladder_3_carry, fulladder_4_carry, fulladder_5_carry,
       fulladder_6_carry, fulladder_7_carry, fulladder_8_carry, fulladder_9_carry, fulladder_10_carry,
       fulladder_11_carry, fulladder_12_carry, fulladder_13_carry, fulladder_14_carry, fulladder_15_carry,
       halfadder_1_carry;

  HalfAdder halfadder_1 (.a(a16[0]), .b(b16[0]), .sum(out16[0]), .carry(halfadder_1_carry));
  FullAdder fulladder_1 (.carry(fulladder_1_carry), .sum(out16[1]), .c(halfadder_1_carry), .b(b16[1]), .a(a16[1]));
  FullAdder fulladder_2 (.carry(fulladder_2_carry), .sum(out16[2]), .c(fulladder_1_carry), .b(b16[2]), .a(a16[2]));
  FullAdder fulladder_3 (.carry(fulladder_3_carry), .sum(out16[3]), .c(fulladder_2_carry), .b(b16[3]), .a(a16[3]));
  FullAdder fulladder_4 (.carry(fulladder_4_carry), .sum(out16[4]), .c(fulladder_3_carry), .b(b16[4]), .a(a16[4]));
  FullAdder fulladder_5 (.carry(fulladder_5_carry), .sum(out16[5]), .c(fulladder_4_carry), .b(b16[5]), .a(a16[5]));
  FullAdder fulladder_6 (.carry(fulladder_6_carry), .sum(out16[6]), .c(fulladder_5_carry), .b(b16[6]), .a(a16[6]));
  FullAdder fulladder_7 (.carry(fulladder_7_carry), .sum(out16[7]), .c(fulladder_6_carry), .b(b16[7]), .a(a16[7]));
  FullAdder fulladder_8 (.carry(fulladder_8_carry), .sum(out16[8]), .c(fulladder_7_carry), .b(b16[8]), .a(a16[8]));
  FullAdder fulladder_9 (.carry(fulladder_9_carry), .sum(out16[9]), .c(fulladder_8_carry), .b(b16[9]), .a(a16[9]));
  FullAdder fulladder_10 (.carry(fulladder_10_carry), .sum(out16[10]), .c(fulladder_9_carry), .b(b16[10]), .a(a16[10]));
  FullAdder fulladder_11 (
    .carry(fulladder_11_carry), .sum(out16[11]), .c(fulladder_10_carry), .b(b16[11]), .a(a16[11]));
  FullAdder fulladder_12 (
    .carry(fulladder_12_carry), .sum(out16[12]), .c(fulladder_11_carry), .b(b16[12]), .a(a16[12]));
  FullAdder fulladder_13 (
    .carry(fulladder_13_carry), .sum(out16[13]), .c(fulladder_12_carry), .b(b16[13]), .a(a16[13]));
  FullAdder fulladder_14 (
    .carry(fulladder_14_carry), .sum(out16[14]), .c(fulladder_13_carry), .b(b16[14]), .a(a16[14]));
  FullAdder fulladder_15 (
    .carry(fulladder_15_carry), .sum(out16[15]), .c(fulladder_14_carry), .b(b16[15]), .a(a16[15]));
  LED led_1 (.in(fulladder_15_carry));
endmodule

module Inc16 (
);

  wire [15:0] add16_1_out16;

  Add16 add16_1 (.out16(add16_1_out16));  // open: a16, b16
  // Probe on add16_1_out16
endmodule
